// Logisim project project_3.circ as structural Verilog: 2 circuits, main circuit main
module main (
  input  [15:0] switch_2,
  input  [15:0] switch_1,
  input  push_button
);

  wire main_1_out_2, main_1_out_3, main_1_out_4, main_1_out_5, main_2_out_6, main_2_out_7, main_2_out_8,
       main_3_out_2, main_3_out_3, main_3_out_4, main_3_out_5, main_4_out_6, main_4_out_7, main_4_out_8,
       main_5_out_2, main_5_out_3, main_5_out_4, main_5_out_5, main_6_out_6, main_6_out_7, main_6_out_8,
       main_7_out_2, main_7_out_3, main_7_out_4, main_7_out_5, main_8_out_6, main_8_out_7, main_8_out_8,
       main_9_out_2, main_9_out_3, main_9_out_4, main_9_out_5, main_10_out_6, main_10_out_7, main_10_out_8,
       main_11_out_2, main_11_out_3, main_11_out_4, main_11_out_5, main_12_out_6, main_12_out_7,
       main_12_out_8, main_13_out_6, main_13_out_7, main_13_out_8, main_14_out_2, main_14_out_3,
       main_14_out_4, main_14_out_5, main_15_out_6, main_15_out_7, main_15_out_8, main_16_out_2,
       main_16_out_3, main_16_out_4, main_16_out_5;
  wire [3:0] undriven_2, undriven_3;
  wire [15:0] undriven;

  _7_segment_driver_main main_1 (
    .in_1(undriven[15:12]), .out_2(main_1_out_2), .out_3(main_1_out_3), .out_4(main_1_out_4),
    .out_5(main_1_out_5));  // open: out_6, out_7, out_8
  _7_Segment_Display u_7_segment_display_1 (
    .g(main_1_out_5), .f(main_1_out_4), .a(main_1_out_3), .b(main_1_out_2), .e(main_2_out_8),
    .d(main_2_out_7), .c(main_2_out_6));  // open: dp
  _7_segment_driver_main main_2 (
    .in_1(undriven[15:12]), .out_6(main_2_out_6), .out_7(main_2_out_7), .out_8(main_2_out_8));  // open: out_2, out_3, out_4, out_5
  _7_segment_driver_main main_3 (
    .out_2(main_3_out_2), .out_3(main_3_out_3), .out_4(main_3_out_4), .out_5(main_3_out_5));  // open: in_1, out_6, out_7, out_8
  _7_Segment_Display u_7_segment_display_2 (
    .g(main_3_out_5), .f(main_3_out_4), .a(main_3_out_3), .b(main_3_out_2), .e(main_4_out_8),
    .d(main_4_out_7), .c(main_4_out_6));  // open: dp
  _7_segment_driver_main main_4 (
    .out_6(main_4_out_6), .out_7(main_4_out_7), .out_8(main_4_out_8));  // open: in_1, out_2, out_3, out_4, out_5
  _7_segment_driver_main main_5 (
    .in_1(undriven_3), .out_2(main_5_out_2), .out_3(main_5_out_3), .out_4(main_5_out_4), .out_5(main_5_out_5));  // open: out_6, out_7, out_8
  _7_Segment_Display u_7_segment_display_3 (
    .g(main_5_out_5), .f(main_5_out_4), .a(main_5_out_3), .b(main_5_out_2), .e(main_6_out_8),
    .d(main_6_out_7), .c(main_6_out_6));  // open: dp
  _7_segment_driver_main main_6 (
    .in_1(undriven_3), .out_6(main_6_out_6), .out_7(main_6_out_7), .out_8(main_6_out_8));  // open: out_2, out_3, out_4, out_5
  _7_segment_driver_main main_7 (
    .out_2(main_7_out_2), .out_3(main_7_out_3), .out_4(main_7_out_4), .out_5(main_7_out_5));  // open: in_1, out_6, out_7, out_8
  _7_Segment_Display u_7_segment_display_4 (
    .g(main_7_out_5), .f(main_7_out_4), .a(main_7_out_3), .b(main_7_out_2), .e(main_8_out_8),
    .d(main_8_out_7), .c(main_8_out_6));  // open: dp
  _7_segment_driver_main main_8 (
    .out_6(main_8_out_6), .out_7(main_8_out_7), .out_8(main_8_out_8));  // open: in_1, out_2, out_3, out_4, out_5
  _7_segment_driver_main main_9 (
    .in_1(undriven_2), .out_2(main_9_out_2), .out_3(main_9_out_3), .out_4(main_9_out_4), .out_5(main_9_out_5));  // open: out_6, out_7, out_8
  _7_Segment_Display u_7_segment_display_5 (
    .g(main_9_out_5), .f(main_9_out_4), .a(main_9_out_3), .b(main_9_out_2), .e(main_10_out_8),
    .d(main_10_out_7), .c(main_10_out_6));  // open: dp
  _7_segment_driver_main main_10 (
    .in_1(undriven_2), .out_6(main_10_out_6), .out_7(main_10_out_7), .out_8(main_10_out_8));  // open: out_2, out_3, out_4, out_5
  _7_segment_driver_main main_11 (
    .out_2(main_11_out_2), .out_3(main_11_out_3), .out_4(main_11_out_4), .out_5(main_11_out_5));  // open: in_1, out_6, out_7, out_8
  _7_Segment_Display u_7_segment_display_6 (
    .g(main_11_out_5), .f(main_11_out_4), .a(main_11_out_3), .b(main_11_out_2), .e(main_12_out_8),
    .d(main_12_out_7), .c(main_12_out_6));  // open: dp
  _7_segment_driver_main main_12 (
    .out_6(main_12_out_6), .out_7(main_12_out_7), .out_8(main_12_out_8));  // open: in_1, out_2, out_3, out_4, out_5
  _7_segment_driver_main main_13 (
    .out_6(main_13_out_6), .out_7(main_13_out_7), .out_8(main_13_out_8));  // open: in_1, out_2, out_3, out_4, out_5
  _7_segment_driver_main main_14 (
    .in_1(undriven[3:0]), .out_2(main_14_out_2), .out_3(main_14_out_3), .out_4(main_14_out_4),
    .out_5(main_14_out_5));  // open: out_6, out_7, out_8
  _7_Segment_Display u_7_segment_display_7 (
    .g(main_14_out_5), .f(main_14_out_4), .a(main_14_out_3), .b(main_14_out_2), .e(main_15_out_8),
    .d(main_15_out_7), .c(main_15_out_6));  // open: dp
  _7_segment_driver_main main_15 (
    .in_1(undriven[3:0]), .out_6(main_15_out_6), .out_7(main_15_out_7), .out_8(main_15_out_8));  // open: out_2, out_3, out_4, out_5
  _7_segment_driver_main main_16 (
    .out_2(main_16_out_2), .out_3(main_16_out_3), .out_4(main_16_out_4), .out_5(main_16_out_5));  // open: in_1, out_6, out_7, out_8
  _7_Segment_Display u_7_segment_display_8 (
    .g(main_16_out_5), .f(main_16_out_4), .a(main_16_out_3), .b(main_16_out_2), .e(main_13_out_8),
    .d(main_13_out_7), .c(main_13_out_6));  // open: dp
endmodule

module timer (
  output TIME_INT,
  output [15:0] TIME
);

  wire clock_1_out;
  wire [10:0] counter_1_q;

  Clock clock_1 (.out(clock_1_out));
  Counter #(.width(12), .max('hfff)) counter_1 (
    .count(clock_1_out), .Q({TIME_INT, counter_1_q}), .clk(clock_1_out), .clr(TIME_INT));  // open: load, D, carry
  Counter #(.width(16), .max('hffff)) counter_2 (
    .count(TIME_INT), .Q(TIME), .clk(TIME_INT));  // open: load, D, carry, clr
endmodule
